// Logisim project D1.circ as structural Verilog: 7 circuits, main circuit main
module main (
  input  B,
  input  B_2,
  input  B_3,
  input  A,
  input  A_2,
  input  A_3,
  input  B_4,
  input  A_4,
  input  B_5,
  input  A_5,
  input  A_6
);

  wire ic7400_nand_1_out_12, ic7402_nor_1_out_12, ic7404_not_1_out_11, ic7408_and_1_out_12,
       ic7432_or_1_out_12, ic7486_xor_1_out_12;

  IC7408__AND ic7408_and_1 (
    .in_3(A), .in_4(B), .out_12(ic7408_and_1_out_12));  // open: in_1, in_2, in_7, in_8, in_9, in_10, out_11, out_13, out_14, in_6, in_5
  LED led_1 (.in(ic7408_and_1_out_12));
  IC7486__XOR ic7486_xor_1 (
    .in_3(A_5), .in_4(B_4), .out_12(ic7486_xor_1_out_12));  // open: in_1, in_2, in_5, in_6, in_7, in_8, in_9, in_10, out_11, out_13, out_14
  LED led_2 (.in(ic7486_xor_1_out_12));
  IC7432__OR ic7432_or_1 (
    .in_3(A_2), .in_4(B_2), .out_12(ic7432_or_1_out_12));  // open: in_1, in_2, in_5, in_6, in_7, in_8, in_9, in_10, out_11, out_13, out_14
  LED led_3 (.in(ic7432_or_1_out_12));
  IC7404__NOT ic7404_not_1 (
    .in_3(A_4), .out_11(ic7404_not_1_out_11));  // open: in_1, in_2, in_4, in_5, in_6, in_7, in_8, out_9, out_10, out_12, out_13, out_14
  LED led_4 (.in(ic7404_not_1_out_11));
  IC7400__NAND ic7400_nand_1 (
    .in_3(A_3), .in_4(B_3), .out_12(ic7400_nand_1_out_12));  // open: in_1, in_2, in_5, in_6, in_7, in_8, in_9, in_10, out_11, out_13, out_14
  LED led_5 (.in(ic7400_nand_1_out_12));
  IC7402__NOR ic7402_nor_1 (
    .in_3(A_6), .in_4(B_5), .out_12(ic7402_nor_1_out_12));  // open: in_1, in_2, in_5, in_6, in_7, in_8, in_9, in_10, out_11, out_13, out_14
  LED led_6 (.in(ic7402_nor_1_out_12));

  // Notes on the sheet:
  //   F
  //   F
  //   F
  //   F
  //   F
  //   F
endmodule

module IC7408__AND (
  input  in_1,
  input  in_2,
  input  in_3,
  input  in_4,
  input  in_5,
  input  in_6,
  input  in_7,
  input  in_8,
  input  in_9,
  input  in_10,
  output out_11,
  output out_12,
  output out_13,
  output out_14
);

  and and_1 (out_11, in_1, in_2);
  and and_2 (out_12, in_3, in_4);
  and and_3 (out_13, in_7, in_8);
  and and_4 (out_14, in_9, in_10);
endmodule

module IC7432__OR (
  input  in_1,
  input  in_2,
  input  in_3,
  input  in_4,
  input  in_5,
  input  in_6,
  input  in_7,
  input  in_8,
  input  in_9,
  input  in_10,
  output out_11,
  output out_12,
  output out_13,
  output out_14
);

  or or_1 (out_11, in_1, in_2);
  or or_2 (out_12, in_3, in_4);
  or or_3 (out_13, in_7, in_8);
  or or_4 (out_14, in_9, in_10);
endmodule

module IC7400__NAND (
  input  in_1,
  input  in_2,
  input  in_3,
  input  in_4,
  input  in_5,
  input  in_6,
  input  in_7,
  input  in_8,
  input  in_9,
  input  in_10,
  output out_11,
  output out_12,
  output out_13,
  output out_14
);

  nand nand_1 (out_11, in_1, in_2);
  nand nand_2 (out_12, in_3, in_4);
  nand nand_3 (out_13, in_7, in_8);
  nand nand_4 (out_14, in_9, in_10);
endmodule

module IC7486__XOR (
  input  in_1,
  input  in_2,
  input  in_3,
  input  in_4,
  input  in_5,
  input  in_6,
  input  in_7,
  input  in_8,
  input  in_9,
  input  in_10,
  output out_11,
  output out_12,
  output out_13,
  output out_14
);

  xor xor_1 (out_11, in_1, in_2);
  xor xor_2 (out_12, in_3, in_4);
  xor xor_3 (out_13, in_7, in_8);
  xor xor_4 (out_14, in_9, in_10);
endmodule

module IC7404__NOT (
  input  in_1,
  input  in_2,
  input  in_3,
  input  in_4,
  input  in_5,
  input  in_6,
  input  in_7,
  input  in_8,
  output out_9,
  output out_10,
  output out_11,
  output out_12,
  output out_13,
  output out_14
);

  not not_1 (out_9, in_1);
  not not_2 (out_10, in_2);
  not not_3 (out_11, in_3);
  not not_4 (out_12, in_6);
  not not_5 (out_13, in_7);
  not not_6 (out_14, in_8);
endmodule

module IC7402__NOR (
  input  in_1,
  input  in_2,
  input  in_3,
  input  in_4,
  input  in_5,
  input  in_6,
  input  in_7,
  input  in_8,
  input  in_9,
  input  in_10,
  output out_11,
  output out_12,
  output out_13,
  output out_14
);

  nor nor_1 (out_11, in_1, in_2);
  nor nor_2 (out_12, in_3, in_4);
  nor nor_3 (out_13, in_7, in_8);
  nor nor_4 (out_14, in_9, in_10);
endmodule
