// Logisim project D2.circ as structural Verilog: 3 circuits, main circuit main
module main (
  input  B,
  input  C,
  input  B_2,
  input  C_2,
  input  A,
  input  A_2
);

  wire ic7408_and_1_out_12, ic7408_and_1_out_14, ic7432_or_1_out_12, ic7432_or_1_out_14;

  IC7408__AND ic7408_and_1 (
    .in_3(A), .in_4(B), .in_9(C), .in_10(ic7408_and_1_out_12), .out_12(ic7408_and_1_out_12),
    .out_14(ic7408_and_1_out_14));  // open: in_1, in_2, in_7, in_8, out_11, out_13, in_6, in_5
  LED led_1 (.in(ic7408_and_1_out_14));
  IC7432__OR ic7432_or_1 (
    .in_3(A_2), .in_4(B_2), .in_9(C_2), .in_10(ic7432_or_1_out_12), .out_12(ic7432_or_1_out_12),
    .out_14(ic7432_or_1_out_14));  // open: in_1, in_2, in_5, in_6, in_7, in_8, out_11, out_13
  LED led_2 (.in(ic7432_or_1_out_14));

  // Notes on the sheet:
  //   F
  //   F
endmodule

module IC7408__AND (
  input  in_1,
  input  in_2,
  input  in_3,
  input  in_4,
  input  in_5,
  input  in_6,
  input  in_7,
  input  in_8,
  input  in_9,
  input  in_10,
  output out_11,
  output out_12,
  output out_13,
  output out_14
);

  and and_1 (out_11, in_1, in_2);
  and and_2 (out_12, in_3, in_4);
  and and_3 (out_13, in_7, in_8);
  and and_4 (out_14, in_9, in_10);
endmodule

module IC7432__OR (
  input  in_1,
  input  in_2,
  input  in_3,
  input  in_4,
  input  in_5,
  input  in_6,
  input  in_7,
  input  in_8,
  input  in_9,
  input  in_10,
  output out_11,
  output out_12,
  output out_13,
  output out_14
);

  or or_1 (out_11, in_1, in_2);
  or or_2 (out_12, in_3, in_4);
  or or_3 (out_13, in_7, in_8);
  or or_4 (out_14, in_9, in_10);
endmodule
