// Logisim project F2.circ as structural Verilog: 7 circuits, main circuit main
module main (
  input  A,
  input  A_2,
  input  B,
  input  A_3,
  input  B_2,
  input  A_4,
  input  B_3,
  input  A_5,
  input  B_4
);

  wire and_1_out_3, not_1_out_2, or_1_out_3, xnor_1_out_3, xor_1_out_3;

  NOT not_1 (.in_1(A), .out_2(not_1_out_2));
  AND and_1 (.in_2(B), .in_1(A_2), .out_3(and_1_out_3));
  OR or_1 (.in_1(A_3), .in_2(B_2), .out_3(or_1_out_3));
  XOR xor_1 (.in_1(A_4), .in_2(B_3), .out_3(xor_1_out_3));
  XNOR xnor_1 (.in_1(A_5), .in_2(B_4), .out_3(xnor_1_out_3));
  LED led_1 (.in(not_1_out_2));
  LED led_2 (.in(and_1_out_3));
  LED led_3 (.in(or_1_out_3));
  LED led_4 (.in(xor_1_out_3));
  LED led_5 (.in(xnor_1_out_3));

  // Notes on the sheet:
  //   F
  //   F
  //   F
  //   F
  //   F
endmodule

module IC7402__NOR (
  input  in_1,
  input  in_2,
  input  in_3,
  input  in_4,
  input  in_5,
  input  in_6,
  input  in_7,
  input  in_8,
  input  in_9,
  input  in_10,
  output out_11,
  output out_12,
  output out_13,
  output out_14
);

  nor nor_1 (out_11, in_1, in_2);
  nor nor_2 (out_12, in_3, in_4);
  nor nor_3 (out_13, in_7, in_8);
  nor nor_4 (out_14, in_9, in_10);
endmodule

module NOT (
  input  in_1,
  output out_2
);

  IC7402__NOR ic7402_nor_1 (
    .in_3(in_1), .in_4(in_1), .out_12(out_2));  // open: in_1, in_2, in_5, in_6, in_7, in_8, in_9, in_10, out_11, out_13, out_14
endmodule

module AND (
  input  in_1,
  input  in_2,
  output out_3
);

  wire ic7402_nor_1_out_12, ic7402_nor_2_out_12;

  IC7402__NOR ic7402_nor_1 (
    .in_3(in_1), .in_4(in_1), .out_12(ic7402_nor_1_out_12));  // open: in_1, in_2, in_5, in_6, in_7, in_8, in_9, in_10, out_11, out_13, out_14
  IC7402__NOR ic7402_nor_2 (
    .in_3(in_2), .in_4(in_2), .out_12(ic7402_nor_2_out_12));  // open: in_1, in_2, in_5, in_6, in_7, in_8, in_9, in_10, out_11, out_13, out_14
  IC7402__NOR ic7402_nor_3 (
    .in_3(ic7402_nor_1_out_12), .in_4(ic7402_nor_2_out_12), .out_12(out_3));  // open: in_1, in_2, in_5, in_6, in_7, in_8, in_9, in_10, out_11, out_13, out_14
endmodule

module OR (
  input  in_1,
  input  in_2,
  output out_3
);

  wire ic7402_nor_1_out_12;

  IC7402__NOR ic7402_nor_1 (
    .in_3(in_1), .in_4(in_2), .out_12(ic7402_nor_1_out_12));  // open: in_1, in_2, in_5, in_6, in_7, in_8, in_9, in_10, out_11, out_13, out_14
  IC7402__NOR ic7402_nor_2 (
    .in_3(ic7402_nor_1_out_12), .in_4(ic7402_nor_1_out_12), .out_12(out_3));  // open: in_1, in_2, in_5, in_6, in_7, in_8, in_9, in_10, out_11, out_13, out_14
endmodule

module XOR (
  input  in_1,
  input  in_2,
  output out_3
);

  wire ic7402_nor_1_out_12, ic7402_nor_2_out_12, ic7402_nor_3_out_12, ic7402_nor_4_out_12;

  IC7402__NOR ic7402_nor_1 (
    .in_3(in_1), .in_4(in_1), .out_12(ic7402_nor_1_out_12));  // open: in_1, in_2, in_5, in_6, in_7, in_8, in_9, in_10, out_11, out_13, out_14
  IC7402__NOR ic7402_nor_2 (
    .in_3(in_2), .in_4(in_2), .out_12(ic7402_nor_2_out_12));  // open: in_1, in_2, in_5, in_6, in_7, in_8, in_9, in_10, out_11, out_13, out_14
  IC7402__NOR ic7402_nor_3 (
    .in_3(ic7402_nor_1_out_12), .in_4(ic7402_nor_2_out_12), .out_12(ic7402_nor_3_out_12));  // open: in_1, in_2, in_5, in_6, in_7, in_8, in_9, in_10, out_11, out_13, out_14
  IC7402__NOR ic7402_nor_4 (
    .in_3(in_1), .in_4(in_2), .out_12(ic7402_nor_4_out_12));  // open: in_1, in_2, in_5, in_6, in_7, in_8, in_9, in_10, out_11, out_13, out_14
  IC7402__NOR ic7402_nor_5 (
    .in_3(ic7402_nor_3_out_12), .in_4(ic7402_nor_4_out_12), .out_12(out_3));  // open: in_1, in_2, in_5, in_6, in_7, in_8, in_9, in_10, out_11, out_13, out_14
endmodule

module XNOR (
  input  in_1,
  input  in_2,
  output out_3
);

  wire ic7402_nor_1_out_12, ic7402_nor_2_out_12, ic7402_nor_3_out_12;

  IC7402__NOR ic7402_nor_1 (
    .in_3(in_1), .in_4(in_2), .out_12(ic7402_nor_1_out_12));  // open: in_1, in_2, in_5, in_6, in_7, in_8, in_9, in_10, out_11, out_13, out_14
  IC7402__NOR ic7402_nor_2 (
    .in_3(in_1), .in_4(ic7402_nor_1_out_12), .out_12(ic7402_nor_2_out_12));  // open: in_1, in_2, in_5, in_6, in_7, in_8, in_9, in_10, out_11, out_13, out_14
  IC7402__NOR ic7402_nor_3 (
    .in_3(ic7402_nor_1_out_12), .in_4(in_2), .out_12(ic7402_nor_3_out_12));  // open: in_1, in_2, in_5, in_6, in_7, in_8, in_9, in_10, out_11, out_13, out_14
  IC7402__NOR ic7402_nor_4 (
    .in_3(ic7402_nor_2_out_12), .in_4(ic7402_nor_3_out_12), .out_12(out_3));  // open: in_1, in_2, in_5, in_6, in_7, in_8, in_9, in_10, out_11, out_13, out_14
endmodule
