// Logisim project F2.circ as structural Verilog: 4 circuits, main circuit main
module main (
  input  A,
  input  B,
  input  C,
  output F
);

  wire ic4075_or_1_out_12, ic4075_or_1_out_13, ic4075_or_1_out_14, ic4075_or_2_out_13, ic4075_or_2_out_14,
       ic7404_not_1_out_12, ic7404_not_1_out_13, ic7404_not_1_out_14, ic7411_and_1_out_12;

  IC4075__OR ic4075_or_1 (
    .in_1(B), .in_2(C), .in_3(ic7404_not_1_out_12), .in_4(B), .in_5(C), .in_6(A), .in_7(ic7404_not_1_out_14),
    .in_8(ic7404_not_1_out_13), .in_9(ic7404_not_1_out_12), .out_12(ic4075_or_1_out_12),
    .out_13(ic4075_or_1_out_13), .out_14(ic4075_or_1_out_14));  // open: in_10, in_11
  IC7404__NOT ic7404_not_1 (
    .in_6(A), .in_7(B), .in_8(C), .out_12(ic7404_not_1_out_12), .out_13(ic7404_not_1_out_13),
    .out_14(ic7404_not_1_out_14));  // open: in_1, in_2, in_3, in_4, in_5, out_9, out_10, out_11
  IC4075__OR ic4075_or_2 (
    .in_4(ic7404_not_1_out_14), .in_5(ic7404_not_1_out_12), .in_6(B), .in_7(ic7404_not_1_out_13),
    .in_8(ic7404_not_1_out_14), .in_9(A), .out_13(ic4075_or_2_out_13), .out_14(ic4075_or_2_out_14));  // open: in_1, in_2, in_3, in_10, in_11, out_12
  IC7411__AND ic7411_and_1 (
    .out_12(ic7411_and_1_out_12), .out_14(F), .in_1(ic4075_or_1_out_12), .in_2(ic4075_or_1_out_13),
    .in_3(ic4075_or_1_out_14), .in_7(ic7411_and_1_out_12), .in_8(ic4075_or_2_out_13),
    .in_9(ic4075_or_2_out_14));  // open: out_13, in_4, in_5, in_6, in_10, in_11
endmodule

module IC7404__NOT (
  input  in_1,
  input  in_2,
  input  in_3,
  input  in_4,
  input  in_5,
  input  in_6,
  input  in_7,
  input  in_8,
  output out_9,
  output out_10,
  output out_11,
  output out_12,
  output out_13,
  output out_14
);

  not not_1 (out_9, in_1);
  not not_2 (out_10, in_2);
  not not_3 (out_11, in_3);
  not not_4 (out_12, in_6);
  not not_5 (out_13, in_7);
  not not_6 (out_14, in_8);
endmodule

module IC7411__AND (
  input  in_1,
  input  in_2,
  input  in_3,
  input  in_4,
  input  in_5,
  input  in_6,
  input  in_7,
  input  in_8,
  input  in_9,
  input  in_10,
  input  in_11,
  output out_12,
  output out_13,
  output out_14
);

  and and_1 (out_12, in_1, in_2, in_3);
  and and_2 (out_13, in_4, in_5, in_6);
  and and_3 (out_14, in_7, in_8, in_9);
endmodule

module IC4075__OR (
  input  in_1,
  input  in_2,
  input  in_3,
  input  in_4,
  input  in_5,
  input  in_6,
  input  in_7,
  input  in_8,
  input  in_9,
  input  in_10,
  input  in_11,
  output out_12,
  output out_13,
  output out_14
);

  or or_1 (out_12, in_1, in_2, in_3);
  or or_2 (out_13, in_4, in_5, in_6);
  or or_3 (out_14, in_7, in_8, in_9);
endmodule
