// Logisim project F2.circ as structural Verilog: 4 circuits, main circuit main
module main (
  input  W,
  input  X,
  input  Y,
  input  Z,
  output A,
  output B,
  output C,
  output D
);

  wire ic4075_or_2_out_13, ic7404_not_1_out_12, ic7404_not_1_out_13, ic7411_and_1_out_12,
       ic7411_and_1_out_13, ic7411_and_2_out_12, ic7411_and_2_out_13, ic7411_and_2_out_14;

  IC4075__OR ic4075_or_1 (
    .in_1(ic7411_and_1_out_12), .in_2(ic7411_and_1_out_12), .in_3(ic7411_and_1_out_13), .out_12(C));  // open: in_4, in_5, in_6, in_7, in_8, in_9, in_10, in_11, out_13, out_14
  IC7411__AND ic7411_and_1 (
    .out_12(ic7411_and_1_out_12), .out_13(ic7411_and_1_out_13), .in_1(Z), .in_2(Z), .in_3(Y), .in_4(D),
    .in_5(ic7404_not_1_out_13), .in_6(ic7404_not_1_out_13));  // open: out_14, in_7, in_8, in_9, in_10, in_11
  IC7411__AND ic7411_and_2 (
    .out_12(ic7411_and_2_out_12), .out_13(ic7411_and_2_out_13), .out_14(ic7411_and_2_out_14),
    .in_1(ic4075_or_2_out_13), .in_2(ic4075_or_2_out_13), .in_3(ic7404_not_1_out_12), .in_4(X), .in_5(X),
    .in_6(ic4075_or_2_out_13), .in_7(X), .in_8(D), .in_9(ic7404_not_1_out_13));  // open: in_10, in_11
  IC4075__OR ic4075_or_2 (
    .in_1(W), .in_2(W), .in_3(ic7411_and_2_out_13), .in_4(Y), .in_5(Y), .in_6(Z), .in_7(ic7411_and_2_out_12),
    .in_8(ic7411_and_2_out_14), .in_9(ic7411_and_2_out_14), .out_12(A), .out_13(ic4075_or_2_out_13),
    .out_14(B));  // open: in_10, in_11
  IC7404__NOT ic7404_not_1 (
    .in_6(X), .in_7(Y), .in_8(Z), .out_12(ic7404_not_1_out_12), .out_13(ic7404_not_1_out_13), .out_14(D));  // open: in_1, in_2, in_3, in_4, in_5, out_9, out_10, out_11
endmodule

module IC7404__NOT (
  input  in_1,
  input  in_2,
  input  in_3,
  input  in_4,
  input  in_5,
  input  in_6,
  input  in_7,
  input  in_8,
  output out_9,
  output out_10,
  output out_11,
  output out_12,
  output out_13,
  output out_14
);

  not not_1 (out_9, in_1);
  not not_2 (out_10, in_2);
  not not_3 (out_11, in_3);
  not not_4 (out_12, in_6);
  not not_5 (out_13, in_7);
  not not_6 (out_14, in_8);
endmodule

module IC7411__AND (
  input  in_1,
  input  in_2,
  input  in_3,
  input  in_4,
  input  in_5,
  input  in_6,
  input  in_7,
  input  in_8,
  input  in_9,
  input  in_10,
  input  in_11,
  output out_12,
  output out_13,
  output out_14
);

  and and_1 (out_12, in_1, in_2, in_3);
  and and_2 (out_13, in_4, in_5, in_6);
  and and_3 (out_14, in_7, in_8, in_9);
endmodule

module IC4075__OR (
  input  in_1,
  input  in_2,
  input  in_3,
  input  in_4,
  input  in_5,
  input  in_6,
  input  in_7,
  input  in_8,
  input  in_9,
  input  in_10,
  input  in_11,
  output out_12,
  output out_13,
  output out_14
);

  or or_1 (out_12, in_1, in_2, in_3);
  or or_2 (out_13, in_4, in_5, in_6);
  or or_3 (out_14, in_7, in_8, in_9);
endmodule
