// Logisim project F1.circ as structural Verilog: 3 circuits, main circuit main
module main (
  input  A4,
  input  A3,
  input  A2,
  input  A1,
  input  B4,
  input  B3,
  input  B2,
  input  B1,
  input  M,
  output [3:0] S,
  output Cout
);

  wire ic7486_xor_1_out_11, ic7486_xor_1_out_12, ic7486_xor_1_out_13, ic7486_xor_1_out_14;

  IC7486__XOR ic7486_xor_1 (
    .in_1(M), .in_2(B1), .in_3(M), .in_4(B2), .in_7(M), .in_8(B4), .in_9(M), .in_10(B3),
    .out_11(ic7486_xor_1_out_11), .out_12(ic7486_xor_1_out_12), .out_13(ic7486_xor_1_out_13),
    .out_14(ic7486_xor_1_out_14));  // open: in_5, in_6
  IC74283__Adder ic74283_adder_1 (
    .A1(A1), .B1(ic7486_xor_1_out_11), .A2(A2), .B2(ic7486_xor_1_out_12), .Cin(M), .S1(S[0]), .A3(A3),
    .B3(ic7486_xor_1_out_14), .A4(A4), .B4(ic7486_xor_1_out_13), .Cout(Cout), .S2(S[1]), .S3(S[2]), .S4(S[3]));  // open: GND, VCC
endmodule

module IC7486__XOR (
  input  in_1,
  input  in_2,
  input  in_3,
  input  in_4,
  input  in_5,
  input  in_6,
  input  in_7,
  input  in_8,
  input  in_9,
  input  in_10,
  output out_11,
  output out_12,
  output out_13,
  output out_14
);

  xor xor_1 (out_11, in_1, in_2);
  xor xor_2 (out_12, in_3, in_4);
  xor xor_3 (out_13, in_7, in_8);
  xor xor_4 (out_14, in_9, in_10);
endmodule

module IC74283__Adder (
  input  Cin,
  input  A1,
  input  B1,
  input  A2,
  input  B2,
  input  A3,
  input  B3,
  input  A4,
  input  B4,
  input  GND,
  input  VCC,
  output S1,
  output S2,
  output S3,
  output S4,
  output Cout
);

  wire adder_1_cout, adder_2_cout, adder_3_cout;

  Adder #(.width(1)) adder_1 (.a(A1), .b(B1), .out(S1), .cin(Cin), .cout(adder_1_cout));
  Adder #(.width(1)) adder_2 (.a(A2), .b(B2), .out(S2), .cin(adder_1_cout), .cout(adder_2_cout));
  Adder #(.width(1)) adder_3 (.a(A3), .b(B3), .out(S3), .cin(adder_2_cout), .cout(adder_3_cout));
  Adder #(.width(1)) adder_4 (.a(A4), .b(B4), .out(S4), .cin(adder_3_cout), .cout(Cout));
endmodule
