// Logisim project F2.circ as structural Verilog: 4 circuits, main circuit main
module main (
  input  A4,
  input  A3,
  input  A2,
  input  A1,
  input  B4,
  input  B3,
  input  B2,
  input  B1,
  output [3:0] S,
  output C
);

  wire ic7408_and_1_out_11, ic7432_or_1_out_13, ic74283_adder_1_cout, ic74283_adder_1_s1, ic74283_adder_1_s2,
       ic74283_adder_1_s3, ic74283_adder_1_s4;

  IC74283__Adder ic74283_adder_1 (
    .A1(A1), .B1(B1), .A2(A2), .B2(B2), .S1(ic74283_adder_1_s1), .A3(A3), .B3(B3), .A4(A4), .B4(B4),
    .Cout(ic74283_adder_1_cout), .S2(ic74283_adder_1_s2), .S3(ic74283_adder_1_s3), .S4(ic74283_adder_1_s4));  // open: Cin, GND, VCC
  IC74283__Adder ic74283_adder_2 (
    .A1(1'b0), .B1(ic74283_adder_1_s1), .A2(C), .B2(ic74283_adder_1_s2), .S1(S[0]), .A3(C),
    .B3(ic74283_adder_1_s3), .A4(1'b0), .B4(ic74283_adder_1_s4), .S2(S[1]), .S3(S[2]), .S4(S[3]));  // open: Cin, Cout, GND, VCC
  IC7408__AND ic7408_and_1 (
    .in_1(ic74283_adder_1_s4), .in_2(ic7432_or_1_out_13), .out_11(ic7408_and_1_out_11));  // open: in_3, in_4, in_7, in_8, in_9, in_10, out_12, out_13, out_14, in_6, in_5
  IC7432__OR ic7432_or_1 (
    .in_7(ic74283_adder_1_s2), .in_8(ic74283_adder_1_s3), .in_9(ic7408_and_1_out_11),
    .in_10(ic74283_adder_1_cout), .out_13(ic7432_or_1_out_13), .out_14(C));  // open: in_1, in_2, in_3, in_4, in_5, in_6, out_11, out_12
endmodule

module IC7408__AND (
  input  in_1,
  input  in_2,
  input  in_3,
  input  in_4,
  input  in_5,
  input  in_6,
  input  in_7,
  input  in_8,
  input  in_9,
  input  in_10,
  output out_11,
  output out_12,
  output out_13,
  output out_14
);

  and and_1 (out_11, in_1, in_2);
  and and_2 (out_12, in_3, in_4);
  and and_3 (out_13, in_7, in_8);
  and and_4 (out_14, in_9, in_10);
endmodule

module IC7432__OR (
  input  in_1,
  input  in_2,
  input  in_3,
  input  in_4,
  input  in_5,
  input  in_6,
  input  in_7,
  input  in_8,
  input  in_9,
  input  in_10,
  output out_11,
  output out_12,
  output out_13,
  output out_14
);

  or or_1 (out_11, in_1, in_2);
  or or_2 (out_12, in_3, in_4);
  or or_3 (out_13, in_7, in_8);
  or or_4 (out_14, in_9, in_10);
endmodule

module IC74283__Adder (
  input  Cin,
  input  A1,
  input  B1,
  input  A2,
  input  B2,
  input  A3,
  input  B3,
  input  A4,
  input  B4,
  input  GND,
  input  VCC,
  output S1,
  output S2,
  output S3,
  output S4,
  output Cout
);

  wire adder_1_cout, adder_2_cout, adder_3_cout;

  Adder #(.width(1)) adder_1 (.a(A1), .b(B1), .out(S1), .cin(Cin), .cout(adder_1_cout));
  Adder #(.width(1)) adder_2 (.a(A2), .b(B2), .out(S2), .cin(adder_1_cout), .cout(adder_2_cout));
  Adder #(.width(1)) adder_3 (.a(A3), .b(B3), .out(S3), .cin(adder_2_cout), .cout(adder_3_cout));
  Adder #(.width(1)) adder_4 (.a(A4), .b(B4), .out(S4), .cin(adder_3_cout), .cout(Cout));
endmodule
