// Logisim project Power Plant Cooling System.circ as structural Verilog: 4 circuits, main circuit main
module main (
  input  S1,
  input  S2,
  input  FS1,
  input  FS2,
  output F1,
  output F2,
  output A
);

  wire ic7404_not_1_out_10, ic7404_not_1_out_12, ic7408_and_1_out_11, ic7408_and_1_out_12,
       ic7408_and_1_out_13, ic7408_and_1_out_14, ic7408_and_2_out_13, ic7408_and_2_out_14,
       ic7432_or_1_out_11, ic7432_or_2_out_11;

  IC7404__NOT ic7404_not_1 (
    .in_2(FS2), .in_6(FS1), .out_10(ic7404_not_1_out_10), .out_12(ic7404_not_1_out_12));  // open: in_1, in_3, in_4, in_5, in_7, in_8, out_9, out_11, out_13, out_14
  IC7408__AND ic7408_and_1 (
    .in_1(ic7404_not_1_out_12), .in_2(ic7404_not_1_out_10), .in_3(ic7408_and_1_out_11),
    .in_4(ic7432_or_1_out_11), .in_7(ic7404_not_1_out_12), .in_8(S1), .in_9(ic7404_not_1_out_10), .in_10(S2),
    .out_11(ic7408_and_1_out_11), .out_12(ic7408_and_1_out_12), .out_13(ic7408_and_1_out_13),
    .out_14(ic7408_and_1_out_14));  // open: in_6, in_5
  IC7432__OR ic7432_or_1 (
    .in_1(S1), .in_2(S2), .in_3(ic7408_and_1_out_12), .in_4(ic7408_and_2_out_14), .in_7(S1),
    .in_8(ic7408_and_1_out_14), .in_9(S2), .in_10(ic7408_and_1_out_13), .out_11(ic7432_or_1_out_11),
    .out_12(A), .out_13(F1), .out_14(F2));  // open: in_5, in_6
  IC7408__AND ic7408_and_2 (
    .in_7(S2), .in_8(S1), .in_9(ic7408_and_2_out_13), .in_10(ic7432_or_2_out_11),
    .out_13(ic7408_and_2_out_13), .out_14(ic7408_and_2_out_14));  // open: in_1, in_2, in_3, in_4, out_11, out_12, in_6, in_5
  IC7432__OR ic7432_or_2 (
    .in_1(ic7404_not_1_out_12), .in_2(ic7404_not_1_out_10), .out_11(ic7432_or_2_out_11));  // open: in_3, in_4, in_5, in_6, in_7, in_8, in_9, in_10, out_12, out_13, out_14
endmodule

module IC7408__AND (
  input  in_1,
  input  in_2,
  input  in_3,
  input  in_4,
  input  in_5,
  input  in_6,
  input  in_7,
  input  in_8,
  input  in_9,
  input  in_10,
  output out_11,
  output out_12,
  output out_13,
  output out_14
);

  and and_1 (out_11, in_1, in_2);
  and and_2 (out_12, in_3, in_4);
  and and_3 (out_13, in_7, in_8);
  and and_4 (out_14, in_9, in_10);
endmodule

module IC7432__OR (
  input  in_1,
  input  in_2,
  input  in_3,
  input  in_4,
  input  in_5,
  input  in_6,
  input  in_7,
  input  in_8,
  input  in_9,
  input  in_10,
  output out_11,
  output out_12,
  output out_13,
  output out_14
);

  or or_1 (out_11, in_1, in_2);
  or or_2 (out_12, in_3, in_4);
  or or_3 (out_13, in_7, in_8);
  or or_4 (out_14, in_9, in_10);
endmodule

module IC7404__NOT (
  input  in_1,
  input  in_2,
  input  in_3,
  input  in_4,
  input  in_5,
  input  in_6,
  input  in_7,
  input  in_8,
  output out_9,
  output out_10,
  output out_11,
  output out_12,
  output out_13,
  output out_14
);

  not not_1 (out_9, in_1);
  not not_2 (out_10, in_2);
  not not_3 (out_11, in_3);
  not not_4 (out_12, in_6);
  not not_5 (out_13, in_7);
  not not_6 (out_14, in_8);
endmodule
